# Fritzing sketch raspberry_picker_pinout (saved by Fritzing 1.0.4)
breadboards: 1

parts:
  Part1 = Arduino Uno (Rev3) - ICSP
  J2 = Basic Servo
  J1 = Basic Servo
  Driver2 = 28BYJ-48 Driver Module [part_number=ULN2003 package=THT]
  SM2 = 28BYJ-48 Stepper Motor [part_number=28BYJ-48]
  R1 = PHOTOCELL [package=photocell-kit]
  R2 = Resistor [tolerance=±5% resistance=10k package="0402 [SMD]"]
  R3 = Resistor [tolerance=±5% resistance=10k package="0402 [SMD]"]
  R4 = Basic Force Sensing Resistor (FSR) [package=THT]
  R5 = Basic Force Sensing Resistor (FSR) [package=THT]
  R6 = Resistor [tolerance=±5% resistance=10k package="0402 [SMD]"]
  Adafruit_HUZZAH_ESP8266_Breakout1 = Adafruit HUZZAH ESP8266 Breakout [part_number=2471]
  Power_plug5 = Power plug
  R7 = Resistor [tolerance=±5% resistance=1k package="0402 [SMD]"]
  R8 = Resistor [tolerance=±5% resistance=2.2k package="0402 [SMD]"]

nets:
  N1: Part1.A3, R5.pin_2, R6.Pin_0
  N2: Part1.A4/SDA, R3.Pin_0, R4.pin_2
  N3: Part1.A5/SCL, R1.P$2, R2.Pin_0
  N4: Part1.ICSP_MOSI, Part1.D11_PWM/MOSI, Driver2.IN1
  N5: Part1.D8, Driver2.IN4
  N6: Part1.D9_PWM, Driver2.IN3
  N7: Part1.D10_PWM/SS, Driver2.IN2
  N8: Part1.D12/MISO, J2.pulse
  N9: Part1.D13/SCK, J1.pulse
  N10: Part1.D3_PWM, Adafruit_HUZZAH_ESP8266_Breakout1.TX
  N11: Part1.D4, R7.Pin_0
  VCC: Part1.5V, J2.vcc, J1.vcc, Driver2.Vmotor, R1.P$1, R4.pin_1, R5.pin_1, Adafruit_HUZZAH_ESP8266_Breakout1.V+, Power_plug5.VCC
  GND: Part1.GND, J2.gnd, J1.gnd, Driver2.GND, R2.Pin_1, R3.Pin_1, R6.Pin_1, Adafruit_HUZZAH_ESP8266_Breakout1.GND, Power_plug5.GND, R8.Pin_1
  N12: Driver2.blue-pin, SM2.blue-pin
  N13: Driver2.pink-pin, SM2.pink-pin
  N14: Driver2.yellow-pin, SM2.yellow-pin
  N15: Driver2.orange-pin, SM2.orange-pin
  N16: Driver2.red-pin, SM2.red-pin
  N17: Adafruit_HUZZAH_ESP8266_Breakout1.RX, R7.Pin_1, R8.Pin_0

notes:
  Light Dependent Resistor
  Servo 1: Sorting
  Servo 2: Door
  Stepper Motor (Driver)
  Force Dependent Resistor 1
  Force Dependent Resistor 2
  5V regulated source
  Voltage divider for 5V-3V3

custom parts:
  28BYJ-48 Driver Module: Generic male header
  28BYJ-48 Stepper Motor: Unipolar Stepper Motor 28BYJ-48 Top coil - pink & orange Bottom coil - blue & yellow Common rail - red Connector pins: blue - pink - yellow - orange - red
